// Logisim project PISO.circ as structural Verilog: 1 circuit, main circuit main
module main (
  input  in_1,
  input  in_2,
  input  in_3,
  input  in_4,
  input  in_5
);

  wire and_1_out, and_2_out, and_3_out, and_4_out, and_5_out, and_6_out, button_1_out, clock_1_out, d_ff_1_q,
       d_ff_2_q, d_ff_3_q, d_ff_4_q, not_1_out, or_1_out, or_2_out, or_3_out;

  not not_1 (not_1_out, in_5);
  Clock clock_1 (.out(clock_1_out));
  Button button_1 (.out(button_1_out));
  D_Flip_Flop d_ff_1 (.clk(clock_1_out), .D(in_1), .Q(d_ff_1_q), .reset(button_1_out));  // open: Qn, preset, en
  and and_1 (and_1_out, d_ff_1_q, d_ff_1_q, in_5);
  or or_1 (or_1_out, and_1_out, and_2_out);
  and and_2 (and_2_out, not_1_out, in_2);
  and and_3 (and_3_out, d_ff_2_q, in_5);
  or or_2 (or_2_out, and_3_out, and_4_out);
  D_Flip_Flop d_ff_2 (.clk(clock_1_out), .D(or_1_out), .Q(d_ff_2_q), .reset(button_1_out));  // open: Qn, preset, en
  and and_4 (and_4_out, not_1_out, not_1_out, in_3);
  and and_5 (and_5_out, d_ff_3_q, in_5);
  and and_6 (and_6_out, not_1_out, in_4);
  D_Flip_Flop d_ff_3 (.clk(clock_1_out), .D(or_2_out), .Q(d_ff_3_q), .reset(button_1_out));  // open: Qn, preset, en
  or or_3 (or_3_out, and_5_out, and_6_out);
  LED led_1 (.in(d_ff_4_q));
  D_Flip_Flop d_ff_4 (.clk(clock_1_out), .D(or_3_out), .Q(d_ff_4_q), .en(button_1_out));  // open: Qn, preset, reset
endmodule
